// Logisim project Project231Final (1).circ as structural Verilog: 1 circuit, main circuit main
module main (
  input  in_1,
  input  [3:0] in_2,
  input  in_3,
  input  in_4,
  input  in_5
);

  wire multiplexer_1_out, multiplexer_2_out, multiplexer_3_out, multiplexer_4_out, multiplexer_5_out,
       multiplexer_6_out, multiplexer_7_out, not_1_out;

  not not_1 (not_1_out, in_1);
  Multiplexer #(.select(4)) multiplexer_1 (
    .in0(in_1), .in1(in_4), .in2(in_4), .in3(not_1_out), .in4(in_3), .in5(in_1), .in6(in_4), .in7(in_3),
    .in8(in_3), .in9(not_1_out), .in10(in_3), .in11(in_3), .in12(in_3), .in13(in_3), .in14(in_3),
    .in15(in_3), .out(multiplexer_1_out), .sel(in_2), .en(in_5));
  Multiplexer #(.select(4)) multiplexer_2 (
    .in0(in_4), .in1(in_4), .in2(in_1), .in3(not_1_out), .in4(in_1), .in5(in_3), .in6(in_4), .in7(in_1),
    .in8(in_3), .in9(in_4), .in10(in_3), .in11(in_3), .in12(in_3), .in13(in_3), .in14(in_3), .in15(in_3),
    .out(multiplexer_2_out), .sel(in_2), .en(in_5));
  Multiplexer #(.select(4)) multiplexer_3 (
    .in0(not_1_out), .in1(in_4), .in2(in_1), .in3(in_3), .in4(in_4), .in5(in_4), .in6(not_1_out), .in7(in_1),
    .in8(in_4), .in9(in_4), .in10(in_3), .in11(in_3), .in12(in_3), .in13(in_3), .in14(in_3), .in15(in_3),
    .out(multiplexer_3_out), .sel(in_2), .en(in_5));
  Multiplexer #(.select(4)) multiplexer_4 (
    .in0(in_4), .in1(in_4), .in2(in_4), .in3(in_3), .in4(not_1_out), .in5(in_4), .in6(in_3), .in7(in_3),
    .in8(in_4), .in9(not_1_out), .in10(in_3), .in11(in_3), .in12(in_3), .in13(in_3), .in14(in_3),
    .in15(in_3), .out(multiplexer_4_out), .sel(in_2), .en(in_5));
  Multiplexer #(.select(4)) multiplexer_5 (
    .in0(in_4), .in1(in_4), .in2(in_4), .in3(not_1_out), .in4(in_4), .in5(not_1_out), .in6(in_3), .in7(in_1),
    .in8(in_4), .in9(in_4), .in10(in_3), .in11(in_3), .in12(in_3), .in13(in_3), .in14(in_3), .in15(in_3),
    .out(multiplexer_5_out), .sel(in_2), .en(in_5));
  Multiplexer #(.select(4)) multiplexer_6 (
    .in0(in_4), .in1(not_1_out), .in2(in_4), .in3(in_3), .in4(in_4), .in5(in_4), .in6(not_1_out), .in7(in_1),
    .in8(in_4), .in9(in_4), .in10(in_3), .in11(in_3), .in12(in_3), .in13(in_3), .in14(in_3), .in15(in_3),
    .out(multiplexer_6_out), .sel(in_2), .en(in_5));
  Multiplexer #(.select(4)) multiplexer_7 (
    .in0(in_4), .in1(in_3), .in2(not_1_out), .in3(in_4), .in4(in_1), .in5(in_4), .in6(not_1_out), .in7(in_4),
    .in8(not_1_out), .in9(in_1), .in10(in_3), .in11(in_3), .in12(in_3), .in13(in_3), .in14(in_3),
    .in15(in_3), .out(multiplexer_7_out), .sel(in_2), .en(in_5));
  _7_Segment_Display u_7_segment_display_1 (
    .g(multiplexer_7_out), .f(multiplexer_5_out), .a(multiplexer_6_out), .b(multiplexer_1_out),
    .e(multiplexer_4_out), .d(multiplexer_3_out), .c(multiplexer_2_out));  // open: dp
endmodule
