// Logisim project Project231Final (2).circ as structural Verilog: 1 circuit, main circuit main
module main (
  input  in_1,
  input  in_2,
  input  in_3,
  input  in_4
);

  wire and_1_out, and_2_out, and_3_out, clock_1_out, j_k_ff_1_q, multiplexer_1_out, multiplexer_2_out,
       multiplexer_3_out, multiplexer_4_out, multiplexer_5_out, multiplexer_6_out, multiplexer_7_out,
       not_1_out;
  wire [3:0] j_k_ff_2_q;

  not not_1 (not_1_out, j_k_ff_1_q);
  Multiplexer #(.select(4)) multiplexer_1 (
    .in0(j_k_ff_1_q), .in1(in_2), .in2(in_2), .in3(not_1_out), .in4(in_1), .in5(j_k_ff_1_q), .in6(in_2),
    .in7(in_1), .in8(in_1), .in9(not_1_out), .in10(in_1), .in11(in_1), .in12(in_1), .in13(in_1), .in14(in_1),
    .in15(in_1), .out(multiplexer_1_out), .sel(j_k_ff_2_q), .en(in_3));
  Multiplexer #(.select(4)) multiplexer_2 (
    .in0(in_2), .in1(in_2), .in2(j_k_ff_1_q), .in3(not_1_out), .in4(j_k_ff_1_q), .in5(in_1), .in6(in_2),
    .in7(j_k_ff_1_q), .in8(in_1), .in9(in_2), .in10(in_1), .in11(in_1), .in12(in_1), .in13(in_1),
    .in14(in_1), .in15(in_1), .out(multiplexer_2_out), .sel(j_k_ff_2_q), .en(in_3));
  Multiplexer #(.select(4)) multiplexer_3 (
    .in0(not_1_out), .in1(in_2), .in2(j_k_ff_1_q), .in3(in_1), .in4(in_2), .in5(in_2), .in6(not_1_out),
    .in7(j_k_ff_1_q), .in8(in_2), .in9(in_2), .in10(in_1), .in11(in_1), .in12(in_1), .in13(in_1),
    .in14(in_1), .in15(in_1), .out(multiplexer_3_out), .sel(j_k_ff_2_q), .en(in_3));
  Multiplexer #(.select(4)) multiplexer_4 (
    .in0(in_2), .in1(in_2), .in2(in_2), .in3(in_1), .in4(not_1_out), .in5(in_2), .in6(in_1), .in7(in_1),
    .in8(in_2), .in9(not_1_out), .in10(in_1), .in11(in_1), .in12(in_1), .in13(in_1), .in14(in_1),
    .in15(in_1), .out(multiplexer_4_out), .sel(j_k_ff_2_q), .en(in_3));
  Multiplexer #(.select(4)) multiplexer_5 (
    .in0(in_2), .in1(in_2), .in2(in_2), .in3(not_1_out), .in4(in_2), .in5(not_1_out), .in6(in_1),
    .in7(j_k_ff_1_q), .in8(in_2), .in9(in_2), .in10(in_1), .in11(in_1), .in12(in_1), .in13(in_1),
    .in14(in_1), .in15(in_1), .out(multiplexer_5_out), .sel(j_k_ff_2_q), .en(in_3));
  Multiplexer #(.select(4)) multiplexer_6 (
    .in0(in_2), .in1(not_1_out), .in2(in_2), .in3(in_1), .in4(in_2), .in5(in_2), .in6(not_1_out),
    .in7(j_k_ff_1_q), .in8(in_2), .in9(in_2), .in10(in_1), .in11(in_1), .in12(in_1), .in13(in_1),
    .in14(in_1), .in15(in_1), .out(multiplexer_6_out), .sel(j_k_ff_2_q), .en(in_3));
  Multiplexer #(.select(4)) multiplexer_7 (
    .in0(in_2), .in1(in_1), .in2(not_1_out), .in3(in_2), .in4(j_k_ff_1_q), .in5(in_2), .in6(not_1_out),
    .in7(in_2), .in8(not_1_out), .in9(j_k_ff_1_q), .in10(in_1), .in11(in_1), .in12(in_1), .in13(in_1),
    .in14(in_1), .in15(in_1), .out(multiplexer_7_out), .sel(j_k_ff_2_q), .en(in_3));
  Clock clock_1 (.out(clock_1_out));
  J_K_Flip_Flop j_k_ff_1 (.J(in_4), .clk(clock_1_out), .K(in_4), .Q(j_k_ff_1_q));  // open: Qn, preset, en, reset
  and and_1 (and_1_out, j_k_ff_1_q, j_k_ff_2_q[0]);
  J_K_Flip_Flop j_k_ff_2 (
    .J(j_k_ff_1_q), .clk(clock_1_out), .K(j_k_ff_1_q), .Q(j_k_ff_2_q[0]));  // open: Qn, preset, en, reset
  J_K_Flip_Flop j_k_ff_3 (
    .J(and_1_out), .clk(clock_1_out), .K(and_1_out), .Q(j_k_ff_2_q[1]));  // open: Qn, preset, en, reset
  and and_2 (and_2_out, and_1_out, j_k_ff_2_q[1]);
  J_K_Flip_Flop j_k_ff_4 (
    .J(and_2_out), .clk(clock_1_out), .K(and_2_out), .Q(j_k_ff_2_q[2]));  // open: Qn, preset, en, reset
  and and_3 (and_3_out, and_2_out, j_k_ff_2_q[2]);
  J_K_Flip_Flop j_k_ff_5 (
    .J(and_3_out), .clk(clock_1_out), .K(and_3_out), .Q(j_k_ff_2_q[3]));  // open: Qn, preset, en, reset
  _7_Segment_Display u_7_segment_display_1 (
    .g(multiplexer_7_out), .f(multiplexer_5_out), .a(multiplexer_6_out), .b(multiplexer_1_out),
    .e(multiplexer_4_out), .d(multiplexer_3_out), .c(multiplexer_2_out));  // open: dp
endmodule
